// Digital circuit CPU.dig as structural Verilog
module CPU (
  input  [15:0] inM,
  input  [15:0] instruction,
  input  reset
);

  wire [15:0] A_Register_q, alu16_1_out, D_Register_q, multiplexer_1_out;

  Register #(.Bits(16)) A_Register (.Q(A_Register_q));  // open: D, C, en
  Multiplexer #(.Bits(16)) multiplexer_1 (
    .sel(instruction[12]), .in_0(A_Register_q), .in_1(inM), .out(multiplexer_1_out));
  Register #(.Bits(16)) D_Register (.D(alu16_1_out), .en(instruction[4]), .Q(D_Register_q));  // open: C
  alu16 alu16_1 (
    .zx(instruction[11]), .nx(instruction[10]), .zy(instruction[9]), .ny(instruction[8]), .f(instruction[7]),
    .no(instruction[6]), .out(alu16_1_out), .x(D_Register_q), .y(multiplexer_1_out));  // open: zr, ng
endmodule
