// Digital circuit HackComputer.dig as structural Verilog
module HackComputer (
  input  reset,
  input  clk
);

  wire cpu_1_writem;
  wire [15:0] cpu_1_addressm, cpu_1_outm, cpu_1_pc, ramasync_1_q, rom_1_d;

  RAMAsync #(.AddrBits(16), .Bits(16)) ramasync_1 (
    .A(cpu_1_addressm), .D(cpu_1_outm), .we(cpu_1_writem), .Q(ramasync_1_q));
  ROM #(.AddrBits(16), .Bits(16)) rom_1 (.A(cpu_1_pc), .sel(1'b1), .D(rom_1_d));
  CPU cpu_1 (
    .clock(clk), .inM(ramasync_1_q), .instruction(rom_1_d), .reset(reset), .outM(cpu_1_outm),
    .writeM(cpu_1_writem), .pc(cpu_1_pc), .addressM(cpu_1_addressm));

  // Notes on the sheet:
  //   clk: Hz: 10
  //   contents of rom_1 (hex, n*v repeats v):
  //   5,ec10,0,e308,10,efc8,11,ea88,10,fc10,0,f4d0,19,e301,11,fc10,10
  //   ,f090,11,e308,10,fc10,e7c8,8,ea87,11,fc10,1,e308,1d,ea87
endmodule
